// Logisim project BST_2502_Kochkin_lab1_task2.circ as structural Verilog: 2 circuits, main circuit main
module main (
  input  A,
  input  B,
  input  C,
  output F
);

  wire and_1_out, and_2_out, and_3_out, not_1_out, or_1_out;

  and and_1 (and_1_out, A, B);
  and and_2 (and_2_out, B, C);
  and and_3 (and_3_out, A, C);
  not not_1 (not_1_out, and_3_out);
  or or_1 (or_1_out, and_1_out, and_2_out);
  or or_2 (F, or_1_out, not_1_out);
endmodule

module main_simplified (
  input  A,
  input  B,
  input  C,
  output F
);

  wire and_1_out, and_2_out, not_1_out;

  not not_1 (not_1_out, B);
  and and_1 (and_1_out, A, not_1_out);
  and and_2 (and_2_out, and_1_out, C);
  not not_2 (F, and_2_out);
endmodule
