// Logisim project BST_2502_Kochkin_lab2_task1.circ as structural Verilog
module main (
  input  x1,
  input  x2,
  input  x3,
  input  x4,
  output f
);

  wire and_1_out, and_2_out, and_3_out, and_4_out, not_1_out, not_2_out, not_3_out, not_4_out, not_5_out,
       or_1_out, or_2_out;

  not not_1 (not_1_out, x2);
  not not_2 (not_2_out, x3);
  and and_1 (and_1_out, x1, not_3_out);
  not not_3 (not_3_out, x2);
  not not_4 (not_4_out, x4);
  not not_5 (not_5_out, x1);
  and and_2 (and_2_out, not_1_out, not_2_out);
  and and_3 (and_3_out, and_1_out, not_4_out);
  and and_4 (and_4_out, x2, x4);
  or or_1 (or_1_out, not_5_out, and_2_out);
  or or_2 (or_2_out, and_3_out, and_4_out);
  or or_3 (f, or_1_out, or_2_out);
endmodule

module Karnaugh (
  input  x1,
  input  x2,
  input  x3,
  input  x4,
  output f
);

  wire and_1_out, and_2_out, and_3_out, not_1_out, not_2_out, not_3_out, not_4_out, not_5_out, or_1_out,
       or_2_out;

  not not_1 (not_1_out, x1);
  and and_1 (and_1_out, x2, x4);
  not not_2 (not_2_out, x2);
  and and_2 (and_2_out, not_2_out, not_3_out);
  not not_3 (not_3_out, x4);
  not not_4 (not_4_out, x2);
  and and_3 (and_3_out, not_4_out, not_5_out);
  not not_5 (not_5_out, x3);
  or or_1 (or_1_out, not_1_out, and_1_out);
  or or_2 (or_2_out, and_2_out, and_3_out);
  or or_3 (f, or_1_out, or_2_out);
endmodule
