// Logisim project BST_2502_Kochkin_lab3_task3.circ as structural Verilog: 1 circuit, main circuit main
module main (
  input  x0,
  input  x1,
  input  x2,
  input  x3,
  input  x4,
  input  x5,
  input  x6,
  input  x7,
  input  x8,
  input  x9,
  input  x10,
  input  x11,
  input  x12,
  input  x13,
  input  x14,
  input  x15,
  output y0,
  output y1,
  output y2,
  output y3
);
endmodule
