// Logisim project BST_2502_Kochkin_lab4_task2.circ as structural Verilog: 1 circuit, main circuit main
module main (
  input  x1,
  input  x2,
  input  x3,
  output y0,
  output y1,
  output y2,
  output y3,
  output y4,
  output y5,
  output y6,
  output y7
);

  wire not_1_out, not_2_out, not_3_out, not_4_out, not_5_out, not_6_out, not_7_out, not_8_out, not_9_out,
       not_10_out, not_11_out, not_12_out;

  not not_1 (not_1_out, x3);
  and and_1 (y1, x1, x2, x3);
  not not_2 (not_2_out, x2);
  not not_3 (not_3_out, x2);
  not not_4 (not_4_out, x3);
  not not_5 (not_5_out, x1);
  not not_6 (not_6_out, x1);
  not not_7 (not_7_out, x2);
  not not_8 (not_8_out, x1);
  not not_9 (not_9_out, x3);
  not not_10 (not_10_out, x1);
  not not_11 (not_11_out, x2);
  not not_12 (not_12_out, x3);
  and and_2 (y0, x1, x2, not_1_out);
  and and_3 (y2, x1, not_2_out, x3);
  and and_4 (y3, x1, not_3_out, not_4_out);
  and and_5 (y4, not_5_out, x2, x3);
  and and_6 (y5, not_6_out, not_7_out, x3);
  and and_7 (y6, not_8_out, x2, not_9_out);
  and and_8 (y7, not_10_out, not_11_out, not_12_out);
endmodule
